// Logisim project Proj2starter.circ as structural Verilog: 4 circuits, main circuit regfile
module CPUmain (
);

  wire control_1_imm_sel, control_1_reg_write_e;
  wire [3:0] control_1_alu_code;
  wire [4:0] control_1_rd, control_1_rs, control_1_rt;
  wire [31:0] alu_1_res, control_1_imm, multiplexer_1_out, regfile_1_rs_data, regfile_1_rt_data;

  regfile regfile_1 (
    .write_e(control_1_reg_write_e), .rd_data(alu_1_res), .rs(control_1_rs), .rt(control_1_rt),
    .rd(control_1_rd), .rs_data(regfile_1_rs_data), .rt_data(regfile_1_rt_data));
  Control control_1 (
    .rs(control_1_rs), .rt(control_1_rt), .rd(control_1_rd), .imm(control_1_imm),
    .reg_write_e(control_1_reg_write_e), .imm_sel(control_1_imm_sel), .ALU_code(control_1_alu_code));  // open: Inst
  Multiplexer #(.width(32)) multiplexer_1 (
    .in0(regfile_1_rs_data), .in1(control_1_imm), .out(multiplexer_1_out), .sel(control_1_imm_sel));
  ALU alu_1 (.OP1(multiplexer_1_out), .OP2(regfile_1_rt_data), .ALU_CODE(control_1_alu_code), .Res(alu_1_res));
endmodule

module regfile (
  input  write_e,
  input  [4:0] rd,
  input  [4:0] rs,
  input  [31:0] rd_data,
  input  [4:0] rt,
  output [31:0] rs_data,
  output [31:0] rt_data
);

  wire clock_1_out, demultiplexer_1_out1, demultiplexer_1_out2, demultiplexer_1_out3, demultiplexer_1_out4,
       demultiplexer_1_out5, demultiplexer_1_out6, demultiplexer_1_out7, demultiplexer_1_out8,
       demultiplexer_1_out9, demultiplexer_1_out10, demultiplexer_1_out11, demultiplexer_1_out12,
       demultiplexer_1_out13, demultiplexer_1_out14, demultiplexer_1_out15, demultiplexer_1_out16,
       demultiplexer_1_out17, demultiplexer_1_out18, demultiplexer_1_out19, demultiplexer_1_out20,
       demultiplexer_1_out21, demultiplexer_1_out22, demultiplexer_1_out23, demultiplexer_1_out24,
       demultiplexer_1_out25, demultiplexer_1_out26, demultiplexer_1_out27, demultiplexer_1_out28,
       demultiplexer_1_out29, demultiplexer_1_out30, demultiplexer_1_out31;
  wire [31:0] demultiplexer_2_out1, demultiplexer_2_out2, demultiplexer_2_out3, demultiplexer_2_out4,
       demultiplexer_2_out5, demultiplexer_2_out6, demultiplexer_2_out7, demultiplexer_2_out8,
       demultiplexer_2_out9, demultiplexer_2_out10, demultiplexer_2_out11, demultiplexer_2_out12,
       demultiplexer_2_out13, demultiplexer_2_out14, demultiplexer_2_out15, demultiplexer_2_out16,
       demultiplexer_2_out17, demultiplexer_2_out18, demultiplexer_2_out19, demultiplexer_2_out20,
       demultiplexer_2_out21, demultiplexer_2_out22, demultiplexer_2_out23, demultiplexer_2_out24,
       demultiplexer_2_out25, demultiplexer_2_out26, demultiplexer_2_out27, demultiplexer_2_out28,
       demultiplexer_2_out29, demultiplexer_2_out30, demultiplexer_2_out31, Reg1_q, Reg2_q, Reg3_q, Reg4_q,
       Reg5_q, Reg6_q, Reg7_q, Reg8_q, Reg9_q, Reg10_q, Reg11_q, Reg12_q, Reg13_q, Reg14_q, Reg15_q, Reg16_q,
       Reg17_q, Reg18_q, Reg19_q, Reg20_q, Reg21_q, Reg22_q, Reg23_q, Reg24_q, Reg25_q, Reg26_q, Reg27_q,
       Reg28_q, Reg29_q, Reg30_q, Reg31_q;

  Demultiplexer #(.select(5)) demultiplexer_1 (
    .out1(demultiplexer_1_out1), .out2(demultiplexer_1_out2), .out3(demultiplexer_1_out3),
    .out4(demultiplexer_1_out4), .out5(demultiplexer_1_out5), .out6(demultiplexer_1_out6),
    .out7(demultiplexer_1_out7), .out8(demultiplexer_1_out8), .out9(demultiplexer_1_out9),
    .out10(demultiplexer_1_out10), .out11(demultiplexer_1_out11), .out12(demultiplexer_1_out12),
    .out13(demultiplexer_1_out13), .out14(demultiplexer_1_out14), .out15(demultiplexer_1_out15),
    .out16(demultiplexer_1_out16), .out17(demultiplexer_1_out17), .out18(demultiplexer_1_out18),
    .out19(demultiplexer_1_out19), .out20(demultiplexer_1_out20), .out21(demultiplexer_1_out21),
    .out22(demultiplexer_1_out22), .out23(demultiplexer_1_out23), .out24(demultiplexer_1_out24),
    .out25(demultiplexer_1_out25), .out26(demultiplexer_1_out26), .out27(demultiplexer_1_out27),
    .out28(demultiplexer_1_out28), .out29(demultiplexer_1_out29), .out30(demultiplexer_1_out30),
    .out31(demultiplexer_1_out31), .in(write_e), .sel(rd));  // open: out0
  Demultiplexer #(.select(5), .width(32)) demultiplexer_2 (
    .out1(demultiplexer_2_out1), .out2(demultiplexer_2_out2), .out3(demultiplexer_2_out3),
    .out4(demultiplexer_2_out4), .out5(demultiplexer_2_out5), .out6(demultiplexer_2_out6),
    .out7(demultiplexer_2_out7), .out8(demultiplexer_2_out8), .out9(demultiplexer_2_out9),
    .out10(demultiplexer_2_out10), .out11(demultiplexer_2_out11), .out12(demultiplexer_2_out12),
    .out13(demultiplexer_2_out13), .out14(demultiplexer_2_out14), .out15(demultiplexer_2_out15),
    .out16(demultiplexer_2_out16), .out17(demultiplexer_2_out17), .out18(demultiplexer_2_out18),
    .out19(demultiplexer_2_out19), .out20(demultiplexer_2_out20), .out21(demultiplexer_2_out21),
    .out22(demultiplexer_2_out22), .out23(demultiplexer_2_out23), .out24(demultiplexer_2_out24),
    .out25(demultiplexer_2_out25), .out26(demultiplexer_2_out26), .out27(demultiplexer_2_out27),
    .out28(demultiplexer_2_out28), .out29(demultiplexer_2_out29), .out30(demultiplexer_2_out30),
    .out31(demultiplexer_2_out31), .in(rd_data), .sel(rd));  // open: out0
  Clock clock_1 (.out(clock_1_out));
  Register #(.width(32)) Reg1 (
    .D(demultiplexer_2_out1), .en(demultiplexer_1_out1), .clk(clock_1_out), .Q(Reg1_q));  // open: clr
  Register #(.width(32)) Reg2 (
    .D(demultiplexer_2_out2), .en(demultiplexer_1_out2), .clk(clock_1_out), .Q(Reg2_q));  // open: clr
  Register #(.width(32)) Reg3 (
    .D(demultiplexer_2_out3), .en(demultiplexer_1_out3), .clk(clock_1_out), .Q(Reg3_q));  // open: clr
  Register #(.width(32)) Reg4 (
    .D(demultiplexer_2_out4), .en(demultiplexer_1_out4), .clk(clock_1_out), .Q(Reg4_q));  // open: clr
  Register #(.width(32)) Reg5 (
    .D(demultiplexer_2_out5), .en(demultiplexer_1_out5), .clk(clock_1_out), .Q(Reg5_q));  // open: clr
  Register #(.width(32)) Reg6 (
    .D(demultiplexer_2_out6), .en(demultiplexer_1_out6), .clk(clock_1_out), .Q(Reg6_q));  // open: clr
  Register #(.width(32)) Reg7 (
    .D(demultiplexer_2_out7), .en(demultiplexer_1_out7), .clk(clock_1_out), .Q(Reg7_q));  // open: clr
  Register #(.width(32)) Reg8 (
    .D(demultiplexer_2_out8), .en(demultiplexer_1_out8), .clk(clock_1_out), .Q(Reg8_q));  // open: clr
  Register #(.width(32)) Reg9 (
    .D(demultiplexer_2_out9), .en(demultiplexer_1_out9), .clk(clock_1_out), .Q(Reg9_q));  // open: clr
  Register #(.width(32)) Reg10 (
    .D(demultiplexer_2_out10), .en(demultiplexer_1_out10), .clk(clock_1_out), .Q(Reg10_q));  // open: clr
  Register #(.width(32)) Reg11 (
    .D(demultiplexer_2_out11), .en(demultiplexer_1_out11), .clk(clock_1_out), .Q(Reg11_q));  // open: clr
  Register #(.width(32)) Reg12 (
    .D(demultiplexer_2_out12), .en(demultiplexer_1_out12), .clk(clock_1_out), .Q(Reg12_q));  // open: clr
  Register #(.width(32)) Reg13 (
    .D(demultiplexer_2_out13), .en(demultiplexer_1_out13), .clk(clock_1_out), .Q(Reg13_q));  // open: clr
  Register #(.width(32)) Reg14 (
    .D(demultiplexer_2_out14), .en(demultiplexer_1_out14), .clk(clock_1_out), .Q(Reg14_q));  // open: clr
  Register #(.width(32)) Reg15 (
    .D(demultiplexer_2_out15), .en(demultiplexer_1_out15), .clk(clock_1_out), .Q(Reg15_q));  // open: clr
  Register #(.width(32)) Reg16 (
    .D(demultiplexer_2_out16), .en(demultiplexer_1_out16), .clk(clock_1_out), .Q(Reg16_q));  // open: clr
  Register #(.width(32)) Reg17 (
    .D(demultiplexer_2_out17), .en(demultiplexer_1_out17), .clk(clock_1_out), .Q(Reg17_q));  // open: clr
  Register #(.width(32)) Reg18 (
    .D(demultiplexer_2_out18), .en(demultiplexer_1_out18), .clk(clock_1_out), .Q(Reg18_q));  // open: clr
  Register #(.width(32)) Reg19 (
    .D(demultiplexer_2_out19), .en(demultiplexer_1_out19), .clk(clock_1_out), .Q(Reg19_q));  // open: clr
  Register #(.width(32)) Reg20 (
    .D(demultiplexer_2_out20), .en(demultiplexer_1_out20), .clk(clock_1_out), .Q(Reg20_q));  // open: clr
  Register #(.width(32)) Reg21 (
    .D(demultiplexer_2_out21), .en(demultiplexer_1_out21), .clk(clock_1_out), .Q(Reg21_q));  // open: clr
  Register #(.width(32)) Reg22 (
    .D(demultiplexer_2_out22), .en(demultiplexer_1_out22), .clk(clock_1_out), .Q(Reg22_q));  // open: clr
  Register #(.width(32)) Reg23 (
    .D(demultiplexer_2_out23), .en(demultiplexer_1_out23), .clk(clock_1_out), .Q(Reg23_q));  // open: clr
  Register #(.width(32)) Reg24 (
    .D(demultiplexer_2_out24), .en(demultiplexer_1_out24), .clk(clock_1_out), .Q(Reg24_q));  // open: clr
  Register #(.width(32)) Reg25 (
    .D(demultiplexer_2_out25), .en(demultiplexer_1_out25), .clk(clock_1_out), .Q(Reg25_q));  // open: clr
  Register #(.width(32)) Reg26 (
    .D(demultiplexer_2_out26), .en(demultiplexer_1_out26), .clk(clock_1_out), .Q(Reg26_q));  // open: clr
  Register #(.width(32)) Reg27 (
    .D(demultiplexer_2_out27), .en(demultiplexer_1_out27), .clk(clock_1_out), .Q(Reg27_q));  // open: clr
  Register #(.width(32)) Reg28 (
    .D(demultiplexer_2_out28), .en(demultiplexer_1_out28), .clk(clock_1_out), .Q(Reg28_q));  // open: clr
  Register #(.width(32)) Reg29 (
    .D(demultiplexer_2_out29), .en(demultiplexer_1_out29), .clk(clock_1_out), .Q(Reg29_q));  // open: clr
  Register #(.width(32)) Reg30 (
    .D(demultiplexer_2_out30), .en(demultiplexer_1_out30), .clk(clock_1_out), .Q(Reg30_q));  // open: clr
  Register #(.width(32)) Reg31 (
    .D(demultiplexer_2_out31), .en(demultiplexer_1_out31), .clk(clock_1_out), .Q(Reg31_q));  // open: clr
  Multiplexer #(.select(5), .width(32)) multiplexer_1 (
    .in0({32{1'b0}}), .in1(Reg1_q), .in2(Reg2_q), .in3(Reg3_q), .in4(Reg4_q), .in5(Reg5_q), .in6(Reg6_q),
    .in7(Reg7_q), .in8(Reg8_q), .in9(Reg9_q), .in10(Reg10_q), .in11(Reg11_q), .in12(Reg12_q), .in13(Reg13_q),
    .in14(Reg14_q), .in15(Reg15_q), .in16(Reg16_q), .in17(Reg17_q), .in18(Reg18_q), .in19(Reg19_q),
    .in20(Reg20_q), .in21(Reg21_q), .in22(Reg22_q), .in23(Reg23_q), .in24(Reg24_q), .in25(Reg25_q),
    .in26(Reg26_q), .in27(Reg27_q), .in28(Reg28_q), .in29(Reg29_q), .in30(Reg30_q), .in31(Reg31_q),
    .out(rs_data), .sel(rs));
  Multiplexer #(.select(5), .width(32)) multiplexer_2 (
    .in0({32{1'b0}}), .in1(Reg1_q), .in2(Reg2_q), .in3(Reg3_q), .in4(Reg4_q), .in5(Reg5_q), .in6(Reg6_q),
    .in7(Reg7_q), .in8(Reg8_q), .in9(Reg9_q), .in10(Reg10_q), .in11(Reg11_q), .in12(Reg12_q), .in13(Reg13_q),
    .in14(Reg14_q), .in15(Reg15_q), .in16(Reg16_q), .in17(Reg17_q), .in18(Reg18_q), .in19(Reg19_q),
    .in20(Reg20_q), .in21(Reg21_q), .in22(Reg22_q), .in23(Reg23_q), .in24(Reg24_q), .in25(Reg25_q),
    .in26(Reg26_q), .in27(Reg27_q), .in28(Reg28_q), .in29(Reg29_q), .in30(Reg30_q), .in31(Reg31_q),
    .out(rt_data), .sel(rt));
endmodule

module ALU (
  input  [3:0] ALU_CODE,
  input  [31:0] OP1,
  input  [31:0] OP2,
  output [31:0] Res
);

  Adder adder_1 ();  // open: a, b, out, cin, cout
  Subtractor subtractor_1 ();  // open: a, b, out, bin, bout
  Multiplier multiplier_1 ();  // open: a, b, out, cin, cout
  Divider divider_1 ();  // open: a, b, out, upper, rem
  Register HI ();  // open: D, en, clk, Q, clr
  Register LO ();  // open: D, en, clk, Q, clr
endmodule

module Control (
  input  [31:0] Inst,
  output [4:0] rs,
  output [4:0] rt,
  output [4:0] rd,
  output [31:0] imm,
  output reg_write_e,
  output imm_sel,
  output [3:0] ALU_code
);
endmodule
