// Logisim project Proj3.circ as structural Verilog: 4 circuits, main circuit regfile
module CPUmain (
);

  wire alu_1_equal, clock_1_out, clock_2_out, control_1_imm_sel, control_1_isj, control_1_isjal,
       control_1_isjr, control_1_mem_load, control_1_mem_write_e, control_1_reg_write_e;
  wire [3:0] control_1_alu_code;
  wire [4:0] control_1_rd, control_1_rs, control_1_rt, control_1_shamt;
  wire [15:0] bit_extender_2_out;
  wire [23:0] bit_extender_4_out;
  wire [25:0] bit_extender_3_out, shifter_2_out;
  wire [31:0] adder_1_out, adder_2_out, alu_1_res, bit_extender_1_out, control_1_imm, multiplexer_1_out,
       multiplexer_2_out, multiplexer_3_out, multiplexer_4_out, multiplexer_5_out, multiplexer_6_out,
       ram_1_dout, regfile_1_rs_data, regfile_1_rt_data, register_1_q, rom_1_data, shifter_1_out,
       shifter_3_out, shifter_4_out;

  Shifter #(.width(32)) shifter_1 (.in(control_1_imm), .\dist (5'b00010), .out(shifter_1_out));
  Adder #(.width(32)) adder_1 (.a(register_1_q), .b(32'h4), .out(adder_1_out));  // open: cin, cout
  Shifter #(.width(26)) shifter_2 (.in(bit_extender_3_out), .\dist (5'b00010), .out(shifter_2_out));
  Multiplexer #(.width(32)) multiplexer_1 (
    .in0(adder_1_out), .in1(adder_2_out), .out(multiplexer_1_out), .sel(alu_1_equal));
  Adder #(.width(32)) adder_2 (.a(adder_1_out), .b(shifter_1_out), .out(adder_2_out));  // open: cin, cout
  assign bit_extender_1_out = {{6{shifter_2_out[25]}}, shifter_2_out};  // Bit_Extender bit_extender_1
  Multiplexer #(.width(32)) multiplexer_2 (
    .in0(bit_extender_1_out), .in1(regfile_1_rs_data), .out(multiplexer_2_out), .sel(control_1_isjr));
  Multiplexer #(.width(32)) multiplexer_3 (
    .in0(multiplexer_1_out), .in1(multiplexer_2_out), .out(multiplexer_3_out), .sel(control_1_isj));
  Shifter #(.shift("lr"), .width(32)) shifter_3 (.in(register_1_q), .\dist (5'b00010), .out(shifter_3_out));
  Bit_Extender #(.in_width(32)) bit_extender_2 (.in(shifter_3_out), .out(bit_extender_2_out));
  Register #(.width(32)) register_1 (
    .D(multiplexer_3_out), .en(1'b1), .clk(clock_1_out), .Q(register_1_q));  // open: clr
  Clock clock_1 (.out(clock_1_out));
  ROM #(.addrWidth(16), .dataWidth(32)) rom_1 (.addr(bit_extender_2_out), .data(rom_1_data));
  Bit_Extender #(.in_width(32), .out_width(26)) bit_extender_3 (.in(rom_1_data), .out(bit_extender_3_out));
  Multiplexer #(.width(32)) multiplexer_4 (
    .in0(alu_1_res), .in1(ram_1_dout), .out(multiplexer_4_out), .sel(control_1_mem_load));
  Multiplexer #(.width(32)) multiplexer_5 (
    .in0(multiplexer_4_out), .in1(adder_1_out), .out(multiplexer_5_out), .sel(control_1_isjal));
  regfile regfile_1 (
    .write_e(control_1_reg_write_e), .rd_data(multiplexer_5_out), .rs(control_1_rs), .rt(control_1_rt),
    .rd(control_1_rd), .rs_data(regfile_1_rs_data), .rt_data(regfile_1_rt_data));
  Control control_1 (
    .Inst(rom_1_data), .isjr(control_1_isjr), .isjal(control_1_isjal), .imm(control_1_imm),
    .ALU_code(control_1_alu_code), .reg_write_e(control_1_reg_write_e), .shamt(control_1_shamt),
    .rt(control_1_rt), .rd(control_1_rd), .rs(control_1_rs), .imm_sel(control_1_imm_sel),
    .mem_load(control_1_mem_load), .mem_write_e(control_1_mem_write_e), .isj(control_1_isj));
  Multiplexer #(.width(32)) multiplexer_6 (
    .in0(regfile_1_rt_data), .in1(control_1_imm), .out(multiplexer_6_out), .sel(control_1_imm_sel));
  ALU alu_1 (
    .ALU_CODE(control_1_alu_code), .OP1(regfile_1_rs_data), .OP2(multiplexer_6_out), .shamt(control_1_shamt),
    .Res(alu_1_res), .equal(alu_1_equal));
  Shifter #(.shift("lr"), .width(32)) shifter_4 (.in(alu_1_res), .\dist (5'b00010), .out(shifter_4_out));
  Bit_Extender #(.in_width(32), .out_width(24)) bit_extender_4 (.in(shifter_4_out), .out(bit_extender_4_out));
  RAM #(.addrWidth(24), .dataWidth(32), .enables("line")) ram_1 (
    .addr(bit_extender_4_out), .we(control_1_mem_write_e), .clk(clock_2_out), .din(regfile_1_rt_data),
    .dout(ram_1_dout));
  Clock clock_2 (.out(clock_2_out));
endmodule

module regfile (
  input  write_e,
  input  [4:0] rd,
  input  [4:0] rs,
  input  [31:0] rd_data,
  input  [4:0] rt,
  output [31:0] rs_data,
  output [31:0] rt_data
);

  wire clock_1_out, demultiplexer_1_out1, demultiplexer_1_out2, demultiplexer_1_out3, demultiplexer_1_out4,
       demultiplexer_1_out5, demultiplexer_1_out6, demultiplexer_1_out7, demultiplexer_1_out8,
       demultiplexer_1_out9, demultiplexer_1_out10, demultiplexer_1_out11, demultiplexer_1_out12,
       demultiplexer_1_out13, demultiplexer_1_out14, demultiplexer_1_out15, demultiplexer_1_out16,
       demultiplexer_1_out17, demultiplexer_1_out18, demultiplexer_1_out19, demultiplexer_1_out20,
       demultiplexer_1_out21, demultiplexer_1_out22, demultiplexer_1_out23, demultiplexer_1_out24,
       demultiplexer_1_out25, demultiplexer_1_out26, demultiplexer_1_out27, demultiplexer_1_out28,
       demultiplexer_1_out29, demultiplexer_1_out30, demultiplexer_1_out31;
  wire [31:0] demultiplexer_2_out1, demultiplexer_2_out2, demultiplexer_2_out3, demultiplexer_2_out4,
       demultiplexer_2_out5, demultiplexer_2_out6, demultiplexer_2_out7, demultiplexer_2_out8,
       demultiplexer_2_out9, demultiplexer_2_out10, demultiplexer_2_out11, demultiplexer_2_out12,
       demultiplexer_2_out13, demultiplexer_2_out14, demultiplexer_2_out15, demultiplexer_2_out16,
       demultiplexer_2_out17, demultiplexer_2_out18, demultiplexer_2_out19, demultiplexer_2_out20,
       demultiplexer_2_out21, demultiplexer_2_out22, demultiplexer_2_out23, demultiplexer_2_out24,
       demultiplexer_2_out25, demultiplexer_2_out26, demultiplexer_2_out27, demultiplexer_2_out28,
       demultiplexer_2_out29, demultiplexer_2_out30, demultiplexer_2_out31, Reg1_q, Reg2_q, Reg3_q, Reg4_q,
       Reg5_q, Reg6_q, Reg7_q, Reg8_q, Reg9_q, Reg10_q, Reg11_q, Reg12_q, Reg13_q, Reg14_q, Reg15_q, Reg16_q,
       Reg17_q, Reg18_q, Reg19_q, Reg20_q, Reg21_q, Reg22_q, Reg23_q, Reg24_q, Reg25_q, Reg26_q, Reg27_q,
       Reg28_q, Reg29_q, Reg30_q, Reg31_q;

  Demultiplexer #(.select(5)) demultiplexer_1 (
    .out1(demultiplexer_1_out1), .out2(demultiplexer_1_out2), .out3(demultiplexer_1_out3),
    .out4(demultiplexer_1_out4), .out5(demultiplexer_1_out5), .out6(demultiplexer_1_out6),
    .out7(demultiplexer_1_out7), .out8(demultiplexer_1_out8), .out9(demultiplexer_1_out9),
    .out10(demultiplexer_1_out10), .out11(demultiplexer_1_out11), .out12(demultiplexer_1_out12),
    .out13(demultiplexer_1_out13), .out14(demultiplexer_1_out14), .out15(demultiplexer_1_out15),
    .out16(demultiplexer_1_out16), .out17(demultiplexer_1_out17), .out18(demultiplexer_1_out18),
    .out19(demultiplexer_1_out19), .out20(demultiplexer_1_out20), .out21(demultiplexer_1_out21),
    .out22(demultiplexer_1_out22), .out23(demultiplexer_1_out23), .out24(demultiplexer_1_out24),
    .out25(demultiplexer_1_out25), .out26(demultiplexer_1_out26), .out27(demultiplexer_1_out27),
    .out28(demultiplexer_1_out28), .out29(demultiplexer_1_out29), .out30(demultiplexer_1_out30),
    .out31(demultiplexer_1_out31), .in(write_e), .sel(rd));  // open: out0
  Demultiplexer #(.select(5), .width(32)) demultiplexer_2 (
    .out1(demultiplexer_2_out1), .out2(demultiplexer_2_out2), .out3(demultiplexer_2_out3),
    .out4(demultiplexer_2_out4), .out5(demultiplexer_2_out5), .out6(demultiplexer_2_out6),
    .out7(demultiplexer_2_out7), .out8(demultiplexer_2_out8), .out9(demultiplexer_2_out9),
    .out10(demultiplexer_2_out10), .out11(demultiplexer_2_out11), .out12(demultiplexer_2_out12),
    .out13(demultiplexer_2_out13), .out14(demultiplexer_2_out14), .out15(demultiplexer_2_out15),
    .out16(demultiplexer_2_out16), .out17(demultiplexer_2_out17), .out18(demultiplexer_2_out18),
    .out19(demultiplexer_2_out19), .out20(demultiplexer_2_out20), .out21(demultiplexer_2_out21),
    .out22(demultiplexer_2_out22), .out23(demultiplexer_2_out23), .out24(demultiplexer_2_out24),
    .out25(demultiplexer_2_out25), .out26(demultiplexer_2_out26), .out27(demultiplexer_2_out27),
    .out28(demultiplexer_2_out28), .out29(demultiplexer_2_out29), .out30(demultiplexer_2_out30),
    .out31(demultiplexer_2_out31), .in(rd_data), .sel(rd));  // open: out0
  Clock clock_1 (.out(clock_1_out));
  Register #(.width(32)) Reg1 (
    .D(demultiplexer_2_out1), .en(demultiplexer_1_out1), .clk(clock_1_out), .Q(Reg1_q));  // open: clr
  Register #(.width(32)) Reg2 (
    .D(demultiplexer_2_out2), .en(demultiplexer_1_out2), .clk(clock_1_out), .Q(Reg2_q));  // open: clr
  Register #(.width(32)) Reg3 (
    .D(demultiplexer_2_out3), .en(demultiplexer_1_out3), .clk(clock_1_out), .Q(Reg3_q));  // open: clr
  Register #(.width(32)) Reg4 (
    .D(demultiplexer_2_out4), .en(demultiplexer_1_out4), .clk(clock_1_out), .Q(Reg4_q));  // open: clr
  Register #(.width(32)) Reg5 (
    .D(demultiplexer_2_out5), .en(demultiplexer_1_out5), .clk(clock_1_out), .Q(Reg5_q));  // open: clr
  Register #(.width(32)) Reg6 (
    .D(demultiplexer_2_out6), .en(demultiplexer_1_out6), .clk(clock_1_out), .Q(Reg6_q));  // open: clr
  Register #(.width(32)) Reg7 (
    .D(demultiplexer_2_out7), .en(demultiplexer_1_out7), .clk(clock_1_out), .Q(Reg7_q));  // open: clr
  Register #(.width(32)) Reg8 (
    .D(demultiplexer_2_out8), .en(demultiplexer_1_out8), .clk(clock_1_out), .Q(Reg8_q));  // open: clr
  Register #(.width(32)) Reg9 (
    .D(demultiplexer_2_out9), .en(demultiplexer_1_out9), .clk(clock_1_out), .Q(Reg9_q));  // open: clr
  Register #(.width(32)) Reg10 (
    .D(demultiplexer_2_out10), .en(demultiplexer_1_out10), .clk(clock_1_out), .Q(Reg10_q));  // open: clr
  Register #(.width(32)) Reg11 (
    .D(demultiplexer_2_out11), .en(demultiplexer_1_out11), .clk(clock_1_out), .Q(Reg11_q));  // open: clr
  Register #(.width(32)) Reg12 (
    .D(demultiplexer_2_out12), .en(demultiplexer_1_out12), .clk(clock_1_out), .Q(Reg12_q));  // open: clr
  Register #(.width(32)) Reg13 (
    .D(demultiplexer_2_out13), .en(demultiplexer_1_out13), .clk(clock_1_out), .Q(Reg13_q));  // open: clr
  Register #(.width(32)) Reg14 (
    .D(demultiplexer_2_out14), .en(demultiplexer_1_out14), .clk(clock_1_out), .Q(Reg14_q));  // open: clr
  Register #(.width(32)) Reg15 (
    .D(demultiplexer_2_out15), .en(demultiplexer_1_out15), .clk(clock_1_out), .Q(Reg15_q));  // open: clr
  Register #(.width(32)) Reg16 (
    .D(demultiplexer_2_out16), .en(demultiplexer_1_out16), .clk(clock_1_out), .Q(Reg16_q));  // open: clr
  Register #(.width(32)) Reg17 (
    .D(demultiplexer_2_out17), .en(demultiplexer_1_out17), .clk(clock_1_out), .Q(Reg17_q));  // open: clr
  Register #(.width(32)) Reg18 (
    .D(demultiplexer_2_out18), .en(demultiplexer_1_out18), .clk(clock_1_out), .Q(Reg18_q));  // open: clr
  Register #(.width(32)) Reg19 (
    .D(demultiplexer_2_out19), .en(demultiplexer_1_out19), .clk(clock_1_out), .Q(Reg19_q));  // open: clr
  Register #(.width(32)) Reg20 (
    .D(demultiplexer_2_out20), .en(demultiplexer_1_out20), .clk(clock_1_out), .Q(Reg20_q));  // open: clr
  Register #(.width(32)) Reg21 (
    .D(demultiplexer_2_out21), .en(demultiplexer_1_out21), .clk(clock_1_out), .Q(Reg21_q));  // open: clr
  Register #(.width(32)) Reg22 (
    .D(demultiplexer_2_out22), .en(demultiplexer_1_out22), .clk(clock_1_out), .Q(Reg22_q));  // open: clr
  Register #(.width(32)) Reg23 (
    .D(demultiplexer_2_out23), .en(demultiplexer_1_out23), .clk(clock_1_out), .Q(Reg23_q));  // open: clr
  Register #(.width(32)) Reg24 (
    .D(demultiplexer_2_out24), .en(demultiplexer_1_out24), .clk(clock_1_out), .Q(Reg24_q));  // open: clr
  Register #(.width(32)) Reg25 (
    .D(demultiplexer_2_out25), .en(demultiplexer_1_out25), .clk(clock_1_out), .Q(Reg25_q));  // open: clr
  Register #(.width(32)) Reg26 (
    .D(demultiplexer_2_out26), .en(demultiplexer_1_out26), .clk(clock_1_out), .Q(Reg26_q));  // open: clr
  Register #(.width(32)) Reg27 (
    .D(demultiplexer_2_out27), .en(demultiplexer_1_out27), .clk(clock_1_out), .Q(Reg27_q));  // open: clr
  Register #(.width(32)) Reg28 (
    .D(demultiplexer_2_out28), .en(demultiplexer_1_out28), .clk(clock_1_out), .Q(Reg28_q));  // open: clr
  Register #(.width(32)) Reg29 (
    .D(demultiplexer_2_out29), .en(demultiplexer_1_out29), .clk(clock_1_out), .Q(Reg29_q));  // open: clr
  Register #(.width(32)) Reg30 (
    .D(demultiplexer_2_out30), .en(demultiplexer_1_out30), .clk(clock_1_out), .Q(Reg30_q));  // open: clr
  Register #(.width(32)) Reg31 (
    .D(demultiplexer_2_out31), .en(demultiplexer_1_out31), .clk(clock_1_out), .Q(Reg31_q));  // open: clr
  Multiplexer #(.select(5), .width(32)) multiplexer_1 (
    .in0({32{1'b0}}), .in1(Reg1_q), .in2(Reg2_q), .in3(Reg3_q), .in4(Reg4_q), .in5(Reg5_q), .in6(Reg6_q),
    .in7(Reg7_q), .in8(Reg8_q), .in9(Reg9_q), .in10(Reg10_q), .in11(Reg11_q), .in12(Reg12_q), .in13(Reg13_q),
    .in14(Reg14_q), .in15(Reg15_q), .in16(Reg16_q), .in17(Reg17_q), .in18(Reg18_q), .in19(Reg19_q),
    .in20(Reg20_q), .in21(Reg21_q), .in22(Reg22_q), .in23(Reg23_q), .in24(Reg24_q), .in25(Reg25_q),
    .in26(Reg26_q), .in27(Reg27_q), .in28(Reg28_q), .in29(Reg29_q), .in30(Reg30_q), .in31(Reg31_q),
    .out(rs_data), .sel(rs));
  Multiplexer #(.select(5), .width(32)) multiplexer_2 (
    .in0({32{1'b0}}), .in1(Reg1_q), .in2(Reg2_q), .in3(Reg3_q), .in4(Reg4_q), .in5(Reg5_q), .in6(Reg6_q),
    .in7(Reg7_q), .in8(Reg8_q), .in9(Reg9_q), .in10(Reg10_q), .in11(Reg11_q), .in12(Reg12_q), .in13(Reg13_q),
    .in14(Reg14_q), .in15(Reg15_q), .in16(Reg16_q), .in17(Reg17_q), .in18(Reg18_q), .in19(Reg19_q),
    .in20(Reg20_q), .in21(Reg21_q), .in22(Reg22_q), .in23(Reg23_q), .in24(Reg24_q), .in25(Reg25_q),
    .in26(Reg26_q), .in27(Reg27_q), .in28(Reg28_q), .in29(Reg29_q), .in30(Reg30_q), .in31(Reg31_q),
    .out(rt_data), .sel(rt));
endmodule

module ALU (
  input  [3:0] ALU_CODE,
  input  [31:0] OP1,
  input  [31:0] OP2,
  input  [4:0] shamt,
  output [31:0] Res,
  output equal
);

  wire and_1_out, and_2_out, clock_1_out, comparator_1_eq, comparator_1_lt, comparator_2_eq, comparator_3_eq,
       comparator_4_eq, comparator_5_eq, not_1_out, or_3_out;
  wire [31:0] adder_1_out, and_3_out, bit_extender_1_out, divider_1_out, divider_1_rem, HI_q, LO_q,
       multiplexer_1_out, multiplexer_2_out, multiplier_1_cout, multiplier_1_out, not_2_out, or_2_out,
       shifter_1_out, shifter_2_out, subtractor_1_out, xor_1_out;

  Comparator #(.mode("unsigned"), .width(32)) comparator_1 (
    .a(OP1), .b(OP2), .eq(comparator_1_eq), .lt(comparator_1_lt));  // open: gt
  and and_1 (and_1_out, comparator_1_eq, comparator_2_eq);
  Comparator #(.mode("unsigned"), .width(4)) comparator_2 (
    .a(ALU_CODE), .b(4'b1101), .eq(comparator_2_eq));  // open: gt, lt
  Comparator #(.mode("unsigned"), .width(4)) comparator_3 (
    .a(4'b1110), .b(ALU_CODE), .eq(comparator_3_eq));  // open: gt, lt
  and and_2 (and_2_out, comparator_3_eq, not_1_out);
  not not_1 (not_1_out, comparator_1_eq);
  Adder #(.width(32)) adder_1 (.a(OP1), .b(OP2), .out(adder_1_out));  // open: cin, cout
  Subtractor #(.width(32)) subtractor_1 (.a(OP1), .b(OP2), .out(subtractor_1_out));  // open: bin, bout
  Multiplier #(.width(32)) multiplier_1 (
    .a(OP1), .b(OP2), .out(multiplier_1_out), .cout(multiplier_1_cout));  // open: cin
  Divider #(.width(32)) divider_1 (.a(OP1), .b(OP2), .out(divider_1_out), .rem(divider_1_rem));  // open: upper
  Shifter #(.width(32)) shifter_1 (.in(OP2), .\dist (shamt), .out(shifter_1_out));
  Shifter #(.shift("lr"), .width(32)) shifter_2 (.in(OP2), .\dist (shamt), .out(shifter_2_out));
  or or_1 (equal, and_1_out, and_2_out);
  assign and_3_out = OP1 & OP2;  // AND_Gate and_3, 32 bits wide
  assign or_2_out = OP1 | OP2;  // OR_Gate or_2, 32 bits wide
  assign xor_1_out = OP1 ^ OP2;  // XOR_Gate xor_1, 32 bits wide
  Multiplexer #(.select(4), .width(32)) multiplexer_1 (
    .in2(multiplier_1_out), .in3(divider_1_out), .out(multiplexer_1_out), .sel(ALU_CODE));  // open: in0, in1, in4, in5, in6, in7, in8, in9, in10, in11, in12, in13, in14, in15
  Multiplexer #(.select(4), .width(32)) multiplexer_2 (
    .in2(multiplier_1_cout), .in3(divider_1_rem), .out(multiplexer_2_out), .sel(ALU_CODE));  // open: in0, in1, in4, in5, in6, in7, in8, in9, in10, in11, in12, in13, in14, in15
  assign not_2_out = ~or_2_out;  // NOT_Gate not_2, 32 bits wide
  Comparator #(.mode("unsigned"), .width(4)) comparator_4 (
    .a(ALU_CODE), .b(4'b0010), .eq(comparator_4_eq));  // open: gt, lt
  Comparator #(.mode("unsigned"), .width(4)) comparator_5 (
    .a(ALU_CODE), .b(4'b0011), .eq(comparator_5_eq));  // open: gt, lt
  Clock clock_1 (.out(clock_1_out));
  or or_3 (or_3_out, comparator_4_eq, comparator_5_eq);
  Register #(.width(32)) LO (.D(multiplexer_1_out), .en(or_3_out), .clk(clock_1_out), .Q(LO_q));  // open: clr
  Register #(.width(32)) HI (.D(multiplexer_2_out), .en(or_3_out), .clk(clock_1_out), .Q(HI_q));  // open: clr
  assign bit_extender_1_out = {{31{1'b0}}, comparator_1_lt};  // Bit_Extender bit_extender_1
  Multiplexer #(.select(4), .width(32)) multiplexer_3 (
    .in0(adder_1_out), .in1(subtractor_1_out), .in4(LO_q), .in5(HI_q), .in6(shifter_1_out),
    .in7(shifter_2_out), .in8(bit_extender_1_out), .in9(and_3_out), .in10(or_2_out), .in11(xor_1_out),
    .in12(not_2_out), .out(Res), .sel(ALU_CODE));  // open: in2, in3, in13, in14, in15
endmodule

module Control (
  input  [31:0] Inst,
  output isjr,
  output isjal,
  output [31:0] imm,
  output [3:0] ALU_code,
  output reg_write_e,
  output [4:0] shamt,
  output [4:0] rt,
  output [4:0] rd,
  output [4:0] rs,
  output imm_sel,
  output mem_load,
  output mem_write_e,
  output isj
);

  wire comparator_1_eq, comparator_2_eq, comparator_3_eq, comparator_4_eq, comparator_7_eq, comparator_8_eq,
       not_2_out, not_3_out, or_3_out;
  wire [4:0] multiplexer_2_out, multiplexer_3_out, multiplexer_4_out, multiplexer_5_out, multiplexer_6_out,
       multiplexer_7_out;

  Comparator #(.mode("unsigned"), .width(6)) comparator_1 (
    .a(Inst[31:26]), .b({6{1'b0}}), .eq(comparator_1_eq));  // open: gt, lt
  Comparator #(.mode("unsigned"), .width(6)) comparator_2 (
    .a(6'b001000), .b(Inst[5:0]), .eq(comparator_2_eq));  // open: gt, lt
  Comparator #(.mode("unsigned"), .width(6)) comparator_3 (
    .a(Inst[5:0]), .b(6'b001001), .eq(comparator_3_eq));  // open: gt, lt
  Comparator #(.width(6)) comparator_4 (.a(Inst[5:0]), .b(6'b001100), .eq(comparator_4_eq));  // open: gt, lt
  not not_1 (imm_sel, comparator_1_eq);
  Comparator #(.mode("unsigned"), .width(6)) comparator_5 (
    .a(6'b100100), .b(Inst[31:26]), .eq(mem_load));  // open: gt, lt
  Comparator #(.mode("unsigned"), .width(6)) comparator_6 (
    .a(6'b101011), .b(Inst[31:26]), .eq(mem_write_e));  // open: gt, lt
  Comparator #(.mode("unsigned"), .width(6)) comparator_7 (
    .a(6'b000010), .b(Inst[31:26]), .eq(comparator_7_eq));  // open: gt, lt
  Comparator #(.mode("unsigned"), .width(6)) comparator_8 (
    .a(Inst[31:26]), .b(6'b000011), .eq(comparator_8_eq));  // open: gt, lt
  or or_1 (isjr, comparator_2_eq, comparator_3_eq);
  or or_2 (isjal, comparator_3_eq, comparator_4_eq, comparator_8_eq);
  assign imm = {{16{Inst[15]}}, Inst[15:0]};  // Bit_Extender bit_extender_1
  Multiplexer #(.width(5)) multiplexer_1 (.in0(Inst[15:11]), .in1(Inst[20:16]), .out(rd), .sel(imm_sel));
  or or_3 (or_3_out, comparator_7_eq, comparator_8_eq);
  or or_4 (isj, isjr, or_3_out);
  Multiplexer #(.enable("true"), .select(5), .width(5)) multiplexer_2 (
    .in0(5'b10000), .in2(5'b10001), .in4(5'b11001), .in5(5'b11010), .in6(5'b11011), .in7(5'b11100),
    .in9(5'b10000), .in10(5'b11000), .in12(5'b10000), .out(multiplexer_2_out), .sel(Inst[4:0]), .en(Inst[5]));  // open: in1, in3, in8, in11, in13, in14, in15, in16, in17, in18, in19, in20, in21, in22, in23, in24, in25, in26, in27, in28, in29, in30, in31
  not not_2 (not_2_out, Inst[5]);
  Multiplexer #(.enable("true"), .select(5), .width(5)) multiplexer_3 (
    .in0(5'b10110), .in2(5'b10111), .in16(5'b10101), .in18(5'b10100), .in24(5'b00010), .in26(5'b00011),
    .out(multiplexer_3_out), .sel(Inst[4:0]), .en(not_2_out));  // open: in1, in3, in4, in5, in6, in7, in8, in9, in10, in11, in12, in13, in14, in15, in17, in19, in20, in21, in22, in23, in25, in27, in28, in29, in30, in31
  Multiplexer #(.enable("true"), .select(5), .width(5)) multiplexer_4 (
    .in3(5'b10000), .in11({5{1'b0}}), .out(multiplexer_4_out), .sel(Inst[30:26]), .en(Inst[31]));  // open: in0, in1, in2, in4, in5, in6, in7, in8, in9, in10, in12, in13, in14, in15, in16, in17, in18, in19, in20, in21, in22, in23, in24, in25, in26, in27, in28, in29, in30, in31
  not not_3 (not_3_out, Inst[31]);
  Multiplexer #(.enable("true"), .select(5), .width(5)) multiplexer_5 (
    .in3(5'b10000), .in4(5'b01101), .in5(5'b01110), .in8(5'b10000), .out(multiplexer_5_out),
    .sel(Inst[30:26]), .en(not_3_out));  // open: in0, in1, in2, in6, in7, in9, in10, in11, in12, in13, in14, in15, in16, in17, in18, in19, in20, in21, in22, in23, in24, in25, in26, in27, in28, in29, in30, in31
  Multiplexer #(.width(5)) multiplexer_6 (
    .in0(multiplexer_2_out), .in1(multiplexer_3_out), .out(multiplexer_6_out), .sel(not_2_out));
  Multiplexer #(.width(5)) multiplexer_7 (
    .in0(multiplexer_4_out), .in1(multiplexer_5_out), .out(multiplexer_7_out), .sel(not_3_out));
  Multiplexer #(.width(5)) multiplexer_8 (
    .in0(multiplexer_6_out), .in1(multiplexer_7_out), .out({reg_write_e, ALU_code}), .sel(imm_sel));

  assign rs = Inst[25:21];
  assign rt = Inst[20:16];
  assign shamt = Inst[10:6];

  // Notes on the sheet:
  //   jr
  //   jalr
  //   lw
  //   sw
  //   j
  //   jal
  //   jalr
  //   jal
  //   or
  //   nor
  //   syscall
  //   bne
  //   add
  //   sub
  //   and
  //   xor
  //   slt
  //   sll
  //   srl
  //   mfhi
  //   mflo
  //   mult
  //   div
  //   lw
  //   sw
  //   beq
  //   addi
endmodule
